# Fritzing sketch led_matrix (saved by Fritzing 0.9.2b)

parts:
  Part1 = Arduino Uno (Rev3)
  LED_Matrix = IC, DIP package, 16 pins [chip_label="LED Matrix"]

nets:
  A0: Part1.A0, LED_Matrix.pin5
  A1: Part1.A1, LED_Matrix.pin6
  A2: Part1.A2, LED_Matrix.pin7
  A3: Part1.A3, LED_Matrix.pin8
  N1: Part1.D8, LED_Matrix.pin2
  N2: Part1.D9_PWM, LED_Matrix.pin1
  N3: Part1.D10_PWM/SS, LED_Matrix.pin13
  N4: Part1.D11_PWM/MOSI, LED_Matrix.pin14
  N5: Part1.D12/MISO, LED_Matrix.pin15
  N6: Part1.D13/SCK, LED_Matrix.pin16
  N7: Part1.D2, LED_Matrix.pin9
  N8: Part1.D3_PWM, LED_Matrix.pin10
  N9: Part1.D4, LED_Matrix.pin11
  N10: Part1.D5_PWM, LED_Matrix.pin12
  N11: Part1.D6_PWM, LED_Matrix.pin4
  N12: Part1.D7, LED_Matrix.pin3
